// Logisim project circuit1c.circ as structural Verilog: 1 circuit, main circuit main
module main (
  input  A,
  input  B,
  input  C,
  output out1,
  output out2
);

  wire and_1_out, and_2_out, not_1_out, not_2_out, not_3_out, not_4_out;

  and and_1 (and_1_out, B, C);
  not not_1 (not_1_out, A);
  and and_2 (and_2_out, not_1_out, not_2_out, not_3_out);
  not not_2 (not_2_out, B);
  not not_3 (not_3_out, C);
  and and_3 (out1, A, not_4_out);
  not not_4 (not_4_out, and_1_out);
  or or_1 (out2, and_1_out, and_2_out);
endmodule
