// Logisim project cpu.circ as structural Verilog: 15 circuits, main circuit main
module main (
  input  [15:0] in_1,
  input  reset
);

  wire alu_1_slt, alu_1_z, ALUinB, and_1_out, and_2_out, Ble, Bne, clk, DMwe, inputE, Jal, Jp, Jr,
       memory_latch_1_oe_latched, memory_latch_1_we_latched, not_1_out, not_2_out, not_3_out, outputE, Rdst,
       Rwd, Rwe, textAvail;
  wire [2:0] ALUop, multiplexer_3_out, multiplexer_4_out, pcdecoder_1_rd, pcdecoder_1_rs, pcdecoder_1_rt,
       pcdecoder_1_shamt;
  wire [3:0] pcdecoder_1_opcode;
  wire [5:0] pcdecoder_1_immediate;
  wire [6:0] keyboardData, Rs;
  wire [11:0] pcdecoder_1_address;
  wire [15:0] add_1_result, add_2_result, alu_1_ouput, dataMem_dout, immediateext_1_extended, InsnMem_data,
       memory_latch_1_address_latched, memory_latch_1_data_in_latched, multiplexer_1_out, multiplexer_2_out,
       multiplexer_5_out, multiplexer_6_out, multiplexer_7_out, multiplexer_8_out, multiplexer_9_out,
       multiplexer_10_out, PC_regout, regs_readdata1, regs_readdata2, zeroext7_1_out12, zeroext12_1_bitsout;

  // Probe on multiplexer_9_out
  not not_1 (not_1_out, clk);
  // Probe on PC_regout
  regMod PC (
    .RegIn(multiplexer_9_out), .enable(1'b1), .clk(not_1_out), .Reset(reset), .globalEnable(1'b1),
    .RegOut(PC_regout));
  ROM #(.addrWidth(16), .dataWidth(16)) InsnMem (.addr(PC_regout), .data(InsnMem_data));
  add add_1 (.result(add_1_result), .B(16'h1), .A(PC_regout));  // open: ovf, sub
  // Probe on InsnMem_data
  Clock u_clk (.out(clk));
  pcDecoder pcdecoder_1 (
    .Shamt(pcdecoder_1_shamt), .Instruction(InsnMem_data), .Rt(pcdecoder_1_rt),
    .Address(pcdecoder_1_address), .Immediate(pcdecoder_1_immediate), .Rd(pcdecoder_1_rd),
    .Rs(pcdecoder_1_rs), .opCode(pcdecoder_1_opcode));
  // Probe on pcdecoder_1_opcode
  // Probe on pcdecoder_1_rs
  // Probe on add_1_result
  Multiplexer #(.width(16), .enable("false")) multiplexer_1 (
    .in0(multiplexer_10_out), .in1(add_1_result), .out(multiplexer_1_out), .sel(Jal));
  Multiplexer #(.width(16), .enable("false")) multiplexer_2 (
    .in0(multiplexer_1_out), .in1(zeroext7_1_out12), .out(multiplexer_2_out), .sel(inputE));
  // Probe on multiplexer_2_out
  // Probe on pcdecoder_1_rt
  // Probe on nothing
  Multiplexer #(.width(3), .enable("false")) multiplexer_3 (
    .in0(pcdecoder_1_rt), .in1(pcdecoder_1_rd), .out(multiplexer_3_out), .sel(Rdst));
  ZeroExt7 zeroext7_1 (.out12(zeroext7_1_out12), .in7(keyboardData), .text(textAvail));
  Multiplexer #(.width(3), .enable("false")) multiplexer_4 (
    .in0(multiplexer_3_out), .in1(3'b111), .out(multiplexer_4_out), .sel(Jal));
  // Probe on add_1_result
  // Probe on multiplexer_10_out
  Control control_1 (
    .ALUop(ALUop), .Rwd(Rwd), .DMwe(DMwe), .Rwe(Rwe), .Ble(Ble), .Jal(Jal), .Rdst(Rdst),
    .opCode(pcdecoder_1_opcode), .Bne(Bne), .ALUinB(ALUinB), .Jp(Jp), .Jr(Jr), .inputE(inputE),
    .outputE(outputE));
  // Probe on zeroext12_1_bitsout
  ZeroExt12 zeroext12_1 (.bitsOut(zeroext12_1_bitsout), .bitsIn(pcdecoder_1_address));
  // Probe on regs_readdata1
  RegisterFile regs (
    .ReadReg2(pcdecoder_1_rt), .WriteData(multiplexer_2_out), .ReadReg1(pcdecoder_1_rs),
    .WriteReg(multiplexer_4_out), .Reset(reset), .clk(clk), .RegWriteEnable(Rwe), .ReadData1(regs_readdata1),
    .ReadData2(regs_readdata2));
  // Probe on regs_readdata2
  // Probe on immediateext_1_extended
  // Probe on ALUop
  immediateExt immediateext_1 (.extended(immediateext_1_extended), .immediate(pcdecoder_1_immediate));
  Multiplexer #(.width(16), .enable("false")) multiplexer_5 (
    .in0(regs_readdata2), .in1(immediateext_1_extended), .out(multiplexer_5_out), .sel(ALUinB));
  // Probe on multiplexer_5_out
  OutputRead outputread_1 (.Rs(regs_readdata1), .RsOut(Rs));
  // Probe on add_1_result
  add add_2 (.result(add_2_result), .B(immediateext_1_extended), .A(add_1_result));  // open: ovf, sub
  Keyboard #(.trigger("falling")) keyboard_1 (
    .clk(clk), .re(inputE), .clr(reset), .avail(textAvail), .data(keyboardData));
  and and_1 (and_1_out, Bne, not_2_out);
  not not_2 (not_2_out, alu_1_z);
  ALU alu_1 (
    .InData2(multiplexer_5_out), .ALUop(ALUop), .ouput(alu_1_ouput), .inData1(regs_readdata1),
    .Shamt(pcdecoder_1_shamt), .z(alu_1_z), .slt(alu_1_slt));  // open: ovf
  // Probe on alu_1_ouput
  // Probe on Rs
  // Probe on multiplexer_9_out
  Multiplexer #(.width(16), .enable("false")) multiplexer_6 (
    .in0(add_1_result), .in1(add_2_result), .out(multiplexer_6_out), .sel(and_1_out));
  not not_3 (not_3_out, clk);
  TTY #(.rows(13), .cols(80)) tty_1 (.data(Rs), .clk(clk), .we(outputE), .clr(reset));
  Multiplexer #(.width(16), .enable("false")) multiplexer_7 (
    .in0(multiplexer_6_out), .in1(add_2_result), .out(multiplexer_7_out), .sel(and_2_out));
  and and_2 (and_2_out, Ble, alu_1_slt);
  Multiplexer #(.width(16), .enable("false")) multiplexer_8 (
    .in0(multiplexer_7_out), .in1(zeroext12_1_bitsout), .out(multiplexer_8_out), .sel(Jp));
  memory_latch memory_latch_1 (
    .address(alu_1_ouput), .WE(DMwe), .clk(not_3_out), .data_in(regs_readdata2),
    .address_latched(memory_latch_1_address_latched), .WE_latched(memory_latch_1_we_latched),
    .OE_latched(memory_latch_1_oe_latched), .data_in_latched(memory_latch_1_data_in_latched));
  Multiplexer #(.width(16), .enable("false")) multiplexer_9 (
    .in0(multiplexer_8_out), .in1(regs_readdata1), .out(multiplexer_9_out), .sel(Jr));
  RAM #(.addrWidth(16), .dataWidth(16), .trigger("high"), .databus("bibus")) dataMem (
    .addr(memory_latch_1_address_latched), .we(memory_latch_1_we_latched), .oe(memory_latch_1_oe_latched),
    .din(memory_latch_1_data_in_latched), .dout(dataMem_dout));
  Multiplexer #(.width(16), .enable("false")) multiplexer_10 (
    .in0(alu_1_ouput), .in1(dataMem_dout), .out(multiplexer_10_out), .sel(Rwd));

  // Notes on the sheet:
  //   contents of InsnMem (hex, n*v repeats v):
  //   0 10 1100 1
  //   pc = pc+!
  //   jal
  //   keyboard
  //   bne
  //   data
  //   available
  //   j /jal
  //   jr rs
  //   data out
endmodule

module ALU (
  input  [2:0] ALUop,
  input  [15:0] inData1,
  input  [15:0] InData2,
  input  [2:0] Shamt,
  output ovf,
  output z,
  output slt,
  output [15:0] ouput
);

  wire not_3_out, or_1_out, or_2_out, or_3_out, or_4_out, or_5_out, or_6_out, or_7_out, or_8_out, or_9_out,
       or_10_out, or_11_out, or_12_out, or_13_out, or_14_out, or_15_out;
  wire [15:0] add_1_result, add_2_result, and_1_out, bitshiftl_1_bitsout, bitshiftr_1_bitsout, not_1_out;

  add add_1 (.ovf(ovf), .result(add_1_result), .B(InData2), .sub(1'b0), .A(inData1));
  add add_2 (.result(add_2_result), .B(InData2), .sub(1'b1), .A(inData1));  // open: ovf
  bitShiftL bitshiftl_1 (.bitsIn(inData1), .Shift(Shamt), .bitsOut(bitshiftl_1_bitsout));
  bitShiftR bitshiftr_1 (.bitsIn(inData1), .shift(Shamt), .bitsOut(bitshiftr_1_bitsout));
  assign and_1_out = inData1 & InData2;  // AND_Gate and_1, 16 bits wide
  assign not_1_out = ~inData1;  // NOT_Gate not_1, 16 bits wide
  Multiplexer #(.select(3), .width(16), .enable("false")) multiplexer_1 (
    .in0(add_1_result), .in1(add_2_result), .in2(bitshiftl_1_bitsout), .in3(bitshiftr_1_bitsout),
    .in4(and_1_out), .in5(not_1_out), .out(ouput), .sel(ALUop));  // open: in6, in7
  or or_1 (or_1_out, add_2_result[14], add_2_result[15]);
  or or_2 (or_2_out, add_2_result[10], add_2_result[11]);
  or or_3 (or_3_out, add_2_result[12], add_2_result[13]);
  or or_4 (or_4_out, or_3_out, or_1_out);
  or or_5 (or_5_out, add_2_result[8], add_2_result[9]);
  or or_6 (or_6_out, add_2_result[6], add_2_result[7]);
  or or_7 (or_7_out, or_5_out, or_2_out);
  or or_8 (or_8_out, or_7_out, or_4_out);
  or or_9 (or_9_out, add_2_result[2], add_2_result[3]);
  or or_10 (or_10_out, add_2_result[4], add_2_result[5]);
  or or_11 (or_11_out, or_10_out, or_6_out);
  or or_12 (or_12_out, add_2_result[0], add_2_result[1]);
  or or_13 (or_13_out, or_12_out, or_9_out);
  or or_14 (or_14_out, or_13_out, or_11_out);
  or or_15 (or_15_out, or_14_out, or_8_out);
  not not_2 (z, or_15_out);
  not not_3 (not_3_out, or_15_out);
  or or_16 (slt, not_3_out, add_2_result[15]);

  // Other names for the same wires on the sheet: in1[15:0] = inData1; in2[15:0] = InData2; Op[2:0] = ALUop
endmodule

module add (
  input  [15:0] A,
  input  sub,
  input  [15:0] B,
  output [15:0] result,
  output ovf
);

  wire B0, B1, B2, B3, B4, B5, B6, B7, B8, B9, B10, B11, B12, B13, B14, B15, bitadd_1_cout, bitadd_2_cout,
       bitadd_3_cout, bitadd_4_cout, bitadd_5_cout, bitadd_6_cout, bitadd_7_cout, bitadd_8_cout,
       bitadd_9_cout, bitadd_10_cout, bitadd_11_cout, bitadd_12_cout, bitadd_13_cout, bitadd_14_cout,
       bitadd_15_cout, bitadd_16_cout;
  wire [15:0] not_1_out;

  assign not_1_out = ~B;  // NOT_Gate not_1, 16 bits wide
  Multiplexer #(.width(16), .enable("false")) multiplexer_1 (
    .in0(B), .in1(not_1_out), .out({B15, B14, B13, B12, B11, B10, B9, B8, B7, B6, B5, B4, B3, B2, B1, B0}),
    .sel(sub));
  bitadd bitadd_1 (.sum(result[0]), .cOUT(bitadd_1_cout), .cIN(sub), .B(B0), .A(A[0]));
  bitadd bitadd_2 (.sum(result[1]), .cOUT(bitadd_2_cout), .cIN(bitadd_1_cout), .B(B1), .A(A[1]));
  bitadd bitadd_3 (.sum(result[2]), .cOUT(bitadd_3_cout), .cIN(bitadd_2_cout), .B(B2), .A(A[2]));
  bitadd bitadd_4 (.sum(result[3]), .cOUT(bitadd_4_cout), .cIN(bitadd_3_cout), .B(B3), .A(A[3]));
  bitadd bitadd_5 (.sum(result[4]), .cOUT(bitadd_5_cout), .cIN(bitadd_4_cout), .B(B4), .A(A[4]));
  bitadd bitadd_6 (.sum(result[5]), .cOUT(bitadd_6_cout), .cIN(bitadd_5_cout), .B(B5), .A(A[5]));
  bitadd bitadd_7 (.sum(result[6]), .cOUT(bitadd_7_cout), .cIN(bitadd_6_cout), .B(B6), .A(A[6]));
  bitadd bitadd_8 (.sum(result[7]), .cOUT(bitadd_8_cout), .cIN(bitadd_7_cout), .B(B7), .A(A[7]));
  bitadd bitadd_9 (.sum(result[8]), .cOUT(bitadd_9_cout), .cIN(bitadd_8_cout), .B(B8), .A(A[8]));
  bitadd bitadd_10 (.sum(result[9]), .cOUT(bitadd_10_cout), .cIN(bitadd_9_cout), .B(B9), .A(A[9]));
  bitadd bitadd_11 (.sum(result[10]), .cOUT(bitadd_11_cout), .cIN(bitadd_10_cout), .B(B10), .A(A[10]));
  bitadd bitadd_12 (.sum(result[11]), .cOUT(bitadd_12_cout), .cIN(bitadd_11_cout), .B(B11), .A(A[11]));
  bitadd bitadd_13 (.sum(result[12]), .cOUT(bitadd_13_cout), .cIN(bitadd_12_cout), .B(B12), .A(A[12]));
  bitadd bitadd_14 (.sum(result[13]), .cOUT(bitadd_14_cout), .cIN(bitadd_13_cout), .B(B13), .A(A[13]));
  bitadd bitadd_15 (.sum(result[14]), .cOUT(bitadd_15_cout), .cIN(bitadd_14_cout), .B(B14), .A(A[14]));
  bitadd bitadd_16 (.sum(result[15]), .cOUT(bitadd_16_cout), .cIN(bitadd_15_cout), .B(B15), .A(A[15]));
  xor xor_1 (ovf, bitadd_15_cout, bitadd_16_cout);

  // Other names for the same wires on the sheet: check = sub; o0 = result[0]; o1 = result[1]; o2 = result[2];
  //   o3 = result[3]; o4 = result[4]; o5 = result[5]; o6 = result[6]; o7 = result[7]; o8 = result[8]; o9 = result[9];
  //   o10 = result[10]; o11 = result[11]; o12 = result[12]; o13 = result[13]; o14 = result[14]; o15 = result[15]
endmodule

module bitadd (
  input  A,
  input  B,
  input  cIN,
  output cOUT,
  output sum
);

  wire and_1_out, and_2_out, xor_1_out;

  xor xor_1 (xor_1_out, A, B);
  and and_1 (and_1_out, A, B);
  and and_2 (and_2_out, xor_1_out, cIN);
  xor xor_2 (sum, xor_1_out, cIN);
  or or_1 (cOUT, and_1_out, and_2_out);
endmodule

module bitShiftL (
  input  [15:0] bitsIn,
  input  [2:0] Shift,
  output [15:0] bitsOut
);

  wire multiplexer_1_out, multiplexer_2_out, multiplexer_3_out, multiplexer_4_out, multiplexer_5_out,
       multiplexer_6_out, multiplexer_7_out, multiplexer_8_out, multiplexer_9_out, multiplexer_10_out,
       multiplexer_11_out, multiplexer_12_out, multiplexer_13_out, multiplexer_14_out, multiplexer_15_out,
       multiplexer_16_out, multiplexer_17_out, multiplexer_18_out, multiplexer_19_out, multiplexer_20_out,
       multiplexer_21_out, multiplexer_22_out, multiplexer_23_out, multiplexer_24_out, multiplexer_25_out,
       multiplexer_26_out, multiplexer_27_out, multiplexer_28_out, multiplexer_29_out, multiplexer_30_out,
       multiplexer_31_out, multiplexer_32_out;

  Multiplexer #(.enable("false")) multiplexer_1 (
    .in0(bitsIn[15]), .in1(bitsIn[11]), .out(multiplexer_1_out), .sel(Shift[2]));
  Multiplexer #(.enable("false")) multiplexer_2 (
    .in0(bitsIn[14]), .in1(bitsIn[10]), .out(multiplexer_2_out), .sel(Shift[2]));
  Multiplexer #(.enable("false")) multiplexer_3 (
    .in0(bitsIn[13]), .in1(bitsIn[9]), .out(multiplexer_3_out), .sel(Shift[2]));
  Multiplexer #(.enable("false")) multiplexer_4 (
    .in0(bitsIn[12]), .in1(bitsIn[8]), .out(multiplexer_4_out), .sel(Shift[2]));
  Multiplexer #(.enable("false")) multiplexer_5 (
    .in0(bitsIn[11]), .in1(bitsIn[7]), .out(multiplexer_5_out), .sel(Shift[2]));
  Multiplexer #(.enable("false")) multiplexer_6 (
    .in0(bitsIn[10]), .in1(bitsIn[6]), .out(multiplexer_6_out), .sel(Shift[2]));
  Multiplexer #(.enable("false")) multiplexer_7 (
    .in0(bitsIn[9]), .in1(bitsIn[5]), .out(multiplexer_7_out), .sel(Shift[2]));
  Multiplexer #(.enable("false")) multiplexer_8 (
    .in0(bitsIn[8]), .in1(bitsIn[4]), .out(multiplexer_8_out), .sel(Shift[2]));
  Multiplexer #(.enable("false")) multiplexer_9 (
    .in0(bitsIn[7]), .in1(bitsIn[3]), .out(multiplexer_9_out), .sel(Shift[2]));
  Multiplexer #(.enable("false")) multiplexer_10 (
    .in0(bitsIn[6]), .in1(bitsIn[2]), .out(multiplexer_10_out), .sel(Shift[2]));
  Multiplexer #(.enable("false")) multiplexer_11 (
    .in0(bitsIn[5]), .in1(bitsIn[1]), .out(multiplexer_11_out), .sel(Shift[2]));
  Multiplexer #(.enable("false")) multiplexer_12 (
    .in0(bitsIn[4]), .in1(bitsIn[0]), .out(multiplexer_12_out), .sel(Shift[2]));
  Multiplexer #(.enable("false")) multiplexer_13 (
    .in0(bitsIn[3]), .in1(1'b0), .out(multiplexer_13_out), .sel(Shift[2]));
  Multiplexer #(.enable("false")) multiplexer_14 (
    .in0(bitsIn[2]), .in1(1'b0), .out(multiplexer_14_out), .sel(Shift[2]));
  Multiplexer #(.enable("false")) multiplexer_15 (
    .in0(bitsIn[1]), .in1(1'b0), .out(multiplexer_15_out), .sel(Shift[2]));
  Multiplexer #(.enable("false")) multiplexer_16 (
    .in0(bitsIn[0]), .in1(1'b0), .out(multiplexer_16_out), .sel(Shift[2]));
  Multiplexer #(.enable("false")) multiplexer_17 (
    .in0(multiplexer_1_out), .in1(multiplexer_3_out), .out(multiplexer_17_out), .sel(Shift[1]));
  Multiplexer #(.enable("false")) multiplexer_18 (
    .in0(multiplexer_2_out), .in1(multiplexer_4_out), .out(multiplexer_18_out), .sel(Shift[1]));
  Multiplexer #(.enable("false")) multiplexer_19 (
    .in0(multiplexer_3_out), .in1(multiplexer_5_out), .out(multiplexer_19_out), .sel(Shift[1]));
  Multiplexer #(.enable("false")) multiplexer_20 (
    .in0(multiplexer_4_out), .in1(multiplexer_6_out), .out(multiplexer_20_out), .sel(Shift[1]));
  Multiplexer #(.enable("false")) multiplexer_21 (
    .in0(multiplexer_5_out), .in1(multiplexer_7_out), .out(multiplexer_21_out), .sel(Shift[1]));
  Multiplexer #(.enable("false")) multiplexer_22 (
    .in0(multiplexer_6_out), .in1(multiplexer_8_out), .out(multiplexer_22_out), .sel(Shift[1]));
  Multiplexer #(.enable("false")) multiplexer_23 (
    .in0(multiplexer_7_out), .in1(multiplexer_9_out), .out(multiplexer_23_out), .sel(Shift[1]));
  Multiplexer #(.enable("false")) multiplexer_24 (
    .in0(multiplexer_8_out), .in1(multiplexer_10_out), .out(multiplexer_24_out), .sel(Shift[1]));
  Multiplexer #(.enable("false")) multiplexer_25 (
    .in0(multiplexer_9_out), .in1(multiplexer_11_out), .out(multiplexer_25_out), .sel(Shift[1]));
  Multiplexer #(.enable("false")) multiplexer_26 (
    .in0(multiplexer_10_out), .in1(multiplexer_12_out), .out(multiplexer_26_out), .sel(Shift[1]));
  Multiplexer #(.enable("false")) multiplexer_27 (
    .in0(multiplexer_11_out), .in1(multiplexer_13_out), .out(multiplexer_27_out), .sel(Shift[1]));
  Multiplexer #(.enable("false")) multiplexer_28 (
    .in0(multiplexer_12_out), .in1(multiplexer_14_out), .out(multiplexer_28_out), .sel(Shift[1]));
  Multiplexer #(.enable("false")) multiplexer_29 (
    .in0(multiplexer_13_out), .in1(multiplexer_15_out), .out(multiplexer_29_out), .sel(Shift[1]));
  Multiplexer #(.enable("false")) multiplexer_30 (
    .in0(multiplexer_14_out), .in1(multiplexer_16_out), .out(multiplexer_30_out), .sel(Shift[1]));
  Multiplexer #(.enable("false")) multiplexer_31 (
    .in0(multiplexer_15_out), .in1(1'b0), .out(multiplexer_31_out), .sel(Shift[1]));
  Multiplexer #(.enable("false")) multiplexer_32 (
    .in0(multiplexer_16_out), .in1(1'b0), .out(multiplexer_32_out), .sel(Shift[1]));
  Multiplexer #(.enable("false")) multiplexer_33 (
    .in0(multiplexer_17_out), .in1(multiplexer_18_out), .out(bitsOut[15]), .sel(Shift[0]));
  Multiplexer #(.enable("false")) multiplexer_34 (
    .in0(multiplexer_18_out), .in1(multiplexer_19_out), .out(bitsOut[14]), .sel(Shift[0]));
  Multiplexer #(.enable("false")) multiplexer_35 (
    .in0(multiplexer_19_out), .in1(multiplexer_20_out), .out(bitsOut[13]), .sel(Shift[0]));
  Multiplexer #(.enable("false")) multiplexer_36 (
    .in0(multiplexer_20_out), .in1(multiplexer_21_out), .out(bitsOut[12]), .sel(Shift[0]));
  Multiplexer #(.enable("false")) multiplexer_37 (
    .in0(multiplexer_21_out), .in1(multiplexer_22_out), .out(bitsOut[11]), .sel(Shift[0]));
  Multiplexer #(.enable("false")) multiplexer_38 (
    .in0(multiplexer_22_out), .in1(multiplexer_23_out), .out(bitsOut[10]), .sel(Shift[0]));
  Multiplexer #(.enable("false")) multiplexer_39 (
    .in0(multiplexer_23_out), .in1(multiplexer_24_out), .out(bitsOut[9]), .sel(Shift[0]));
  Multiplexer #(.enable("false")) multiplexer_40 (
    .in0(multiplexer_24_out), .in1(multiplexer_25_out), .out(bitsOut[8]), .sel(Shift[0]));
  Multiplexer #(.enable("false")) multiplexer_41 (
    .in0(multiplexer_25_out), .in1(multiplexer_26_out), .out(bitsOut[7]), .sel(Shift[0]));
  Multiplexer #(.enable("false")) multiplexer_42 (
    .in0(multiplexer_26_out), .in1(multiplexer_27_out), .out(bitsOut[6]), .sel(Shift[0]));
  Multiplexer #(.enable("false")) multiplexer_43 (
    .in0(multiplexer_27_out), .in1(multiplexer_28_out), .out(bitsOut[5]), .sel(Shift[0]));
  Multiplexer #(.enable("false")) multiplexer_44 (
    .in0(multiplexer_28_out), .in1(multiplexer_29_out), .out(bitsOut[4]), .sel(Shift[0]));
  Multiplexer #(.enable("false")) multiplexer_45 (
    .in0(multiplexer_29_out), .in1(multiplexer_30_out), .out(bitsOut[3]), .sel(Shift[0]));
  Multiplexer #(.enable("false")) multiplexer_46 (
    .in0(multiplexer_30_out), .in1(multiplexer_31_out), .out(bitsOut[2]), .sel(Shift[0]));
  Multiplexer #(.enable("false")) multiplexer_47 (
    .in0(multiplexer_31_out), .in1(multiplexer_32_out), .out(bitsOut[1]), .sel(Shift[0]));
  Multiplexer #(.enable("false")) multiplexer_48 (
    .in0(multiplexer_32_out), .in1(1'b0), .out(bitsOut[0]), .sel(Shift[0]));

  // Other names for the same wires on the sheet: B0 = bitsIn[0]; B1 = bitsIn[1]; B2 = bitsIn[2]; B3 = bitsIn[3];
  //   B4 = bitsIn[4]; B5 = bitsIn[5]; B6 = bitsIn[6]; B7 = bitsIn[7]; B8 = bitsIn[8]; B9 = bitsIn[9];
  //   B10 = bitsIn[10]; B11 = bitsIn[11]; B12 = bitsIn[12]; B13 = bitsIn[13]; B14 = bitsIn[14]; B15 = bitsIn[15];
  //   o0 = bitsOut[0]; o1 = bitsOut[1]; o2 = bitsOut[2]; o3 = bitsOut[3]; o4 = bitsOut[4]; o5 = bitsOut[5];
  //   o6 = bitsOut[6]; o7 = bitsOut[7]; o8 = bitsOut[8]; o9 = bitsOut[9]; o10 = bitsOut[10]; o11 = bitsOut[11];
  //   o12 = bitsOut[12]; o13 = bitsOut[13]; o14 = bitsOut[14]; o15 = bitsOut[15]; s1 = Shift[0]; s2 = Shift[1];
  //   s3 = Shift[2]
endmodule

module bitShiftR (
  input  [15:0] bitsIn,
  input  [2:0] shift,
  output [15:0] bitsOut
);

  wire multiplexer_1_out, multiplexer_2_out, multiplexer_3_out, multiplexer_4_out, multiplexer_5_out,
       multiplexer_6_out, multiplexer_7_out, multiplexer_8_out, multiplexer_9_out, multiplexer_10_out,
       multiplexer_11_out, multiplexer_12_out, multiplexer_13_out, multiplexer_14_out, multiplexer_15_out,
       multiplexer_16_out, multiplexer_17_out, multiplexer_18_out, multiplexer_19_out, multiplexer_20_out,
       multiplexer_21_out, multiplexer_22_out, multiplexer_23_out, multiplexer_24_out, multiplexer_25_out,
       multiplexer_26_out, multiplexer_27_out, multiplexer_28_out, multiplexer_29_out, multiplexer_30_out,
       multiplexer_31_out, multiplexer_32_out;

  Multiplexer #(.enable("false")) multiplexer_1 (
    .in0(bitsIn[0]), .in1(bitsIn[4]), .out(multiplexer_1_out), .sel(shift[2]));
  Multiplexer #(.enable("false")) multiplexer_2 (
    .in0(bitsIn[1]), .in1(bitsIn[5]), .out(multiplexer_2_out), .sel(shift[2]));
  Multiplexer #(.enable("false")) multiplexer_3 (
    .in0(bitsIn[2]), .in1(bitsIn[6]), .out(multiplexer_3_out), .sel(shift[2]));
  Multiplexer #(.enable("false")) multiplexer_4 (
    .in0(bitsIn[3]), .in1(bitsIn[7]), .out(multiplexer_4_out), .sel(shift[2]));
  Multiplexer #(.enable("false")) multiplexer_5 (
    .in0(bitsIn[4]), .in1(bitsIn[8]), .out(multiplexer_5_out), .sel(shift[2]));
  Multiplexer #(.enable("false")) multiplexer_6 (
    .in0(bitsIn[5]), .in1(bitsIn[9]), .out(multiplexer_6_out), .sel(shift[2]));
  Multiplexer #(.enable("false")) multiplexer_7 (
    .in0(bitsIn[6]), .in1(bitsIn[10]), .out(multiplexer_7_out), .sel(shift[2]));
  Multiplexer #(.enable("false")) multiplexer_8 (
    .in0(bitsIn[7]), .in1(bitsIn[11]), .out(multiplexer_8_out), .sel(shift[2]));
  Multiplexer #(.enable("false")) multiplexer_9 (
    .in0(bitsIn[8]), .in1(bitsIn[12]), .out(multiplexer_9_out), .sel(shift[2]));
  Multiplexer #(.enable("false")) multiplexer_10 (
    .in0(bitsIn[9]), .in1(bitsIn[13]), .out(multiplexer_10_out), .sel(shift[2]));
  Multiplexer #(.enable("false")) multiplexer_11 (
    .in0(bitsIn[10]), .in1(bitsIn[14]), .out(multiplexer_11_out), .sel(shift[2]));
  Multiplexer #(.enable("false")) multiplexer_12 (
    .in0(bitsIn[11]), .in1(bitsIn[15]), .out(multiplexer_12_out), .sel(shift[2]));
  Multiplexer #(.enable("false")) multiplexer_13 (
    .in0(bitsIn[12]), .in1(1'b0), .out(multiplexer_13_out), .sel(shift[2]));
  Multiplexer #(.enable("false")) multiplexer_14 (
    .in0(bitsIn[13]), .in1(1'b0), .out(multiplexer_14_out), .sel(shift[2]));
  Multiplexer #(.enable("false")) multiplexer_15 (
    .in0(bitsIn[14]), .in1(1'b0), .out(multiplexer_15_out), .sel(shift[2]));
  Multiplexer #(.enable("false")) multiplexer_16 (
    .in0(bitsIn[15]), .in1(1'b0), .out(multiplexer_16_out), .sel(shift[2]));
  Multiplexer #(.enable("false")) multiplexer_17 (
    .in0(multiplexer_1_out), .in1(multiplexer_3_out), .out(multiplexer_17_out), .sel(shift[1]));
  Multiplexer #(.enable("false")) multiplexer_18 (
    .in0(multiplexer_2_out), .in1(multiplexer_4_out), .out(multiplexer_18_out), .sel(shift[1]));
  Multiplexer #(.enable("false")) multiplexer_19 (
    .in0(multiplexer_3_out), .in1(multiplexer_5_out), .out(multiplexer_19_out), .sel(shift[1]));
  Multiplexer #(.enable("false")) multiplexer_20 (
    .in0(multiplexer_4_out), .in1(multiplexer_6_out), .out(multiplexer_20_out), .sel(shift[1]));
  Multiplexer #(.enable("false")) multiplexer_21 (
    .in0(multiplexer_5_out), .in1(multiplexer_7_out), .out(multiplexer_21_out), .sel(shift[1]));
  Multiplexer #(.enable("false")) multiplexer_22 (
    .in0(multiplexer_6_out), .in1(multiplexer_8_out), .out(multiplexer_22_out), .sel(shift[1]));
  Multiplexer #(.enable("false")) multiplexer_23 (
    .in0(multiplexer_7_out), .in1(multiplexer_9_out), .out(multiplexer_23_out), .sel(shift[1]));
  Multiplexer #(.enable("false")) multiplexer_24 (
    .in0(multiplexer_8_out), .in1(multiplexer_10_out), .out(multiplexer_24_out), .sel(shift[1]));
  Multiplexer #(.enable("false")) multiplexer_25 (
    .in0(multiplexer_9_out), .in1(multiplexer_11_out), .out(multiplexer_25_out), .sel(shift[1]));
  Multiplexer #(.enable("false")) multiplexer_26 (
    .in0(multiplexer_10_out), .in1(multiplexer_12_out), .out(multiplexer_26_out), .sel(shift[1]));
  Multiplexer #(.enable("false")) multiplexer_27 (
    .in0(multiplexer_11_out), .in1(multiplexer_13_out), .out(multiplexer_27_out), .sel(shift[1]));
  Multiplexer #(.enable("false")) multiplexer_28 (
    .in0(multiplexer_12_out), .in1(multiplexer_14_out), .out(multiplexer_28_out), .sel(shift[1]));
  Multiplexer #(.enable("false")) multiplexer_29 (
    .in0(multiplexer_13_out), .in1(multiplexer_15_out), .out(multiplexer_29_out), .sel(shift[1]));
  Multiplexer #(.enable("false")) multiplexer_30 (
    .in0(multiplexer_14_out), .in1(multiplexer_16_out), .out(multiplexer_30_out), .sel(shift[1]));
  Multiplexer #(.enable("false")) multiplexer_31 (
    .in0(multiplexer_15_out), .in1(1'b0), .out(multiplexer_31_out), .sel(shift[1]));
  Multiplexer #(.enable("false")) multiplexer_32 (
    .in0(multiplexer_16_out), .in1(1'b0), .out(multiplexer_32_out), .sel(shift[1]));
  Multiplexer #(.enable("false")) multiplexer_33 (
    .in0(multiplexer_17_out), .in1(multiplexer_18_out), .out(bitsOut[0]), .sel(shift[0]));
  Multiplexer #(.enable("false")) multiplexer_34 (
    .in0(multiplexer_18_out), .in1(multiplexer_19_out), .out(bitsOut[1]), .sel(shift[0]));
  Multiplexer #(.enable("false")) multiplexer_35 (
    .in0(multiplexer_19_out), .in1(multiplexer_20_out), .out(bitsOut[2]), .sel(shift[0]));
  Multiplexer #(.enable("false")) multiplexer_36 (
    .in0(multiplexer_20_out), .in1(multiplexer_21_out), .out(bitsOut[3]), .sel(shift[0]));
  Multiplexer #(.enable("false")) multiplexer_37 (
    .in0(multiplexer_21_out), .in1(multiplexer_22_out), .out(bitsOut[4]), .sel(shift[0]));
  Multiplexer #(.enable("false")) multiplexer_38 (
    .in0(multiplexer_22_out), .in1(multiplexer_23_out), .out(bitsOut[5]), .sel(shift[0]));
  Multiplexer #(.enable("false")) multiplexer_39 (
    .in0(multiplexer_23_out), .in1(multiplexer_24_out), .out(bitsOut[6]), .sel(shift[0]));
  Multiplexer #(.enable("false")) multiplexer_40 (
    .in0(multiplexer_24_out), .in1(multiplexer_25_out), .out(bitsOut[7]), .sel(shift[0]));
  Multiplexer #(.enable("false")) multiplexer_41 (
    .in0(multiplexer_25_out), .in1(multiplexer_26_out), .out(bitsOut[8]), .sel(shift[0]));
  Multiplexer #(.enable("false")) multiplexer_42 (
    .in0(multiplexer_26_out), .in1(multiplexer_27_out), .out(bitsOut[9]), .sel(shift[0]));
  Multiplexer #(.enable("false")) multiplexer_43 (
    .in0(multiplexer_27_out), .in1(multiplexer_28_out), .out(bitsOut[10]), .sel(shift[0]));
  Multiplexer #(.enable("false")) multiplexer_44 (
    .in0(multiplexer_28_out), .in1(multiplexer_29_out), .out(bitsOut[11]), .sel(shift[0]));
  Multiplexer #(.enable("false")) multiplexer_45 (
    .in0(multiplexer_29_out), .in1(multiplexer_30_out), .out(bitsOut[12]), .sel(shift[0]));
  Multiplexer #(.enable("false")) multiplexer_46 (
    .in0(multiplexer_30_out), .in1(multiplexer_31_out), .out(bitsOut[13]), .sel(shift[0]));
  Multiplexer #(.enable("false")) multiplexer_47 (
    .in0(multiplexer_31_out), .in1(multiplexer_32_out), .out(bitsOut[14]), .sel(shift[0]));
  Multiplexer #(.enable("false")) multiplexer_48 (
    .in0(multiplexer_32_out), .in1(1'b0), .out(bitsOut[15]), .sel(shift[0]));

  // Other names for the same wires on the sheet: B0 = bitsIn[0]; B1 = bitsIn[1]; B2 = bitsIn[2]; B3 = bitsIn[3];
  //   B4 = bitsIn[4]; B5 = bitsIn[5]; B6 = bitsIn[6]; B7 = bitsIn[7]; B8 = bitsIn[8]; B9 = bitsIn[9];
  //   B10 = bitsIn[10]; B11 = bitsIn[11]; B12 = bitsIn[12]; B13 = bitsIn[13]; B14 = bitsIn[14]; B15 = bitsIn[15];
  //   o0 = bitsOut[0]; o1 = bitsOut[1]; o2 = bitsOut[2]; o3 = bitsOut[3]; o4 = bitsOut[4]; o5 = bitsOut[5];
  //   o6 = bitsOut[6]; o7 = bitsOut[7]; o8 = bitsOut[8]; o9 = bitsOut[9]; o10 = bitsOut[10]; o11 = bitsOut[11];
  //   o12 = bitsOut[12]; o13 = bitsOut[13]; o14 = bitsOut[14]; o15 = bitsOut[15]; s1 = shift[0]; s2 = shift[1];
  //   s3 = shift[2]
endmodule

module RegisterFile (
  input  [15:0] WriteData,
  input  [2:0] WriteReg,
  input  Reset,
  input  [2:0] ReadReg1,
  input  [2:0] ReadReg2,
  input  RegWriteEnable,
  input  clk,
  output [15:0] ReadData1,
  output [15:0] ReadData2
);

  wire En1, En2, En3, En4, En5, En6, En7, En8, r1, r2, r3, r4, r5, r6, r7, r8, r21, r22, r23, r24, r25, r26,
       r27, r28;
  wire [15:0] o1, o2, o3, o4, o5, o6, o7, o8;

  // Probe on WriteData
  regMod regmod_1 (.RegIn(WriteData), .enable(En1), .clk(clk), .Reset(Reset), .globalEnable(1'b0), .RegOut(o1));
  // Probe on o1
  regMod regmod_2 (
    .RegIn(WriteData), .enable(En2), .clk(clk), .Reset(Reset), .globalEnable(RegWriteEnable), .RegOut(o2));
  // Probe on o2
  regMod regmod_3 (
    .RegIn(WriteData), .enable(En3), .clk(clk), .Reset(Reset), .globalEnable(RegWriteEnable), .RegOut(o3));
  // Probe on o3
  regMod regmod_4 (
    .RegIn(WriteData), .enable(En4), .clk(clk), .Reset(Reset), .globalEnable(RegWriteEnable), .RegOut(o4));
  // Probe on o4
  // Probe on WriteData
  regMod regmod_5 (
    .RegIn(WriteData), .enable(En5), .clk(clk), .Reset(Reset), .globalEnable(RegWriteEnable), .RegOut(o5));
  regMod regmod_6 (
    .RegIn(WriteData), .enable(En6), .clk(clk), .Reset(Reset), .globalEnable(RegWriteEnable), .RegOut(o6));
  regMod regmod_7 (
    .RegIn(WriteData), .enable(En7), .clk(clk), .Reset(Reset), .globalEnable(RegWriteEnable), .RegOut(o7));
  regMod regmod_8 (
    .RegIn(WriteData), .enable(En8), .clk(clk), .Reset(Reset), .globalEnable(RegWriteEnable), .RegOut(o8));
  // Probe on o5
  // Probe on o6
  // Probe on o7
  // Probe on o8
  Decoder #(.select(3), .enable("false")) decoder_1 (
    .out0(En1), .out1(En2), .out2(En3), .out3(En4), .out4(En5), .out5(En6), .out6(En7), .out7(En8),
    .sel(WriteReg));
  Decoder #(.select(3), .enable("false")) decoder_2 (
    .out0(r1), .out1(r2), .out2(r3), .out3(r4), .out4(r5), .out5(r6), .out6(r7), .out7(r8), .sel(ReadReg1));
  Decoder #(.select(3), .enable("false")) decoder_3 (
    .out0(r21), .out1(r22), .out2(r23), .out3(r24), .out4(r25), .out5(r26), .out6(r27), .out7(r28),
    .sel(ReadReg2));
  assign ReadData1 = r1 ? o1 : 16'bz;  // Controlled_Buffer controlled_buffer_1
  assign ReadData1 = r2 ? o2 : 16'bz;  // Controlled_Buffer controlled_buffer_2
  assign ReadData1 = r3 ? o3 : 16'bz;  // Controlled_Buffer controlled_buffer_3
  assign ReadData1 = r4 ? o4 : 16'bz;  // Controlled_Buffer controlled_buffer_4
  assign ReadData2 = r21 ? o1 : 16'bz;  // Controlled_Buffer controlled_buffer_5
  assign ReadData2 = r22 ? o2 : 16'bz;  // Controlled_Buffer controlled_buffer_6
  assign ReadData2 = r23 ? o3 : 16'bz;  // Controlled_Buffer controlled_buffer_7
  assign ReadData2 = r24 ? o4 : 16'bz;  // Controlled_Buffer controlled_buffer_8
  assign ReadData1 = r5 ? o5 : 16'bz;  // Controlled_Buffer controlled_buffer_9
  assign ReadData1 = r6 ? o6 : 16'bz;  // Controlled_Buffer controlled_buffer_10
  assign ReadData1 = r7 ? o7 : 16'bz;  // Controlled_Buffer controlled_buffer_11
  assign ReadData1 = r8 ? o8 : 16'bz;  // Controlled_Buffer controlled_buffer_12
  assign ReadData2 = r25 ? o5 : 16'bz;  // Controlled_Buffer controlled_buffer_13
  assign ReadData2 = r26 ? o6 : 16'bz;  // Controlled_Buffer controlled_buffer_14
  assign ReadData2 = r27 ? o7 : 16'bz;  // Controlled_Buffer controlled_buffer_15
  assign ReadData2 = r28 ? o8 : 16'bz;  // Controlled_Buffer controlled_buffer_16

  // Other names for the same wires on the sheet: output1[15:0] = ReadData1; output2[15:0] = ReadData1;
  //   output3[15:0] = ReadData1; output4[15:0] = ReadData1; output5[15:0] = ReadData1; output6[15:0] = ReadData1;
  //   output7[15:0] = ReadData1; output8[15:0] = ReadData1; output21[15:0] = ReadData2; output22[15:0] = ReadData2;
  //   output23[15:0] = ReadData2; output24[15:0] = ReadData2; output25[15:0] = ReadData2; output26[15:0] = ReadData2;
  //   output27[15:0] = ReadData2; output28[15:0] = ReadData2; RR1[2:0] = ReadReg1; RR2[2:0] = ReadReg2;
  //   WrData[15:0] = WriteData; WriteChoose[2:0] = WriteReg; WriteEnable = RegWriteEnable
endmodule

module regMod (
  input  [15:0] RegIn,
  input  enable,
  input  clk,
  input  Reset,
  input  globalEnable,
  output [15:0] RegOut
);

  wire and_1_out;

  and and_1 (and_1_out, enable, globalEnable, clk);
  D_Flip_Flop d_ff_1 (.D(RegIn[0]), .clk(and_1_out), .Q(RegOut[0]), .reset(Reset));  // open: Qn, preset
  D_Flip_Flop d_ff_2 (.D(RegIn[1]), .clk(and_1_out), .Q(RegOut[1]), .reset(Reset));  // open: Qn, preset
  D_Flip_Flop d_ff_3 (.D(RegIn[2]), .clk(and_1_out), .Q(RegOut[2]), .reset(Reset));  // open: Qn, preset
  D_Flip_Flop d_ff_4 (.D(RegIn[3]), .clk(and_1_out), .Q(RegOut[3]), .reset(Reset));  // open: Qn, preset
  D_Flip_Flop d_ff_5 (.D(RegIn[4]), .clk(and_1_out), .Q(RegOut[4]), .reset(Reset));  // open: Qn, preset
  D_Flip_Flop d_ff_6 (.D(RegIn[5]), .clk(and_1_out), .Q(RegOut[5]), .reset(Reset));  // open: Qn, preset
  D_Flip_Flop d_ff_7 (.D(RegIn[6]), .clk(and_1_out), .Q(RegOut[6]), .reset(Reset));  // open: Qn, preset
  D_Flip_Flop d_ff_8 (.D(RegIn[7]), .clk(and_1_out), .Q(RegOut[7]), .reset(Reset));  // open: Qn, preset
  D_Flip_Flop d_ff_9 (.D(RegIn[8]), .clk(and_1_out), .Q(RegOut[8]), .reset(Reset));  // open: Qn, preset
  D_Flip_Flop d_ff_10 (.D(RegIn[9]), .clk(and_1_out), .Q(RegOut[9]), .reset(Reset));  // open: Qn, preset
  D_Flip_Flop d_ff_11 (.D(RegIn[10]), .clk(and_1_out), .Q(RegOut[10]), .reset(Reset));  // open: Qn, preset
  D_Flip_Flop d_ff_12 (.D(RegIn[11]), .clk(and_1_out), .Q(RegOut[11]), .reset(Reset));  // open: Qn, preset
  D_Flip_Flop d_ff_13 (.D(RegIn[12]), .clk(and_1_out), .Q(RegOut[12]), .reset(Reset));  // open: Qn, preset
  D_Flip_Flop d_ff_14 (.D(RegIn[13]), .clk(and_1_out), .Q(RegOut[13]), .reset(Reset));  // open: Qn, preset
  D_Flip_Flop d_ff_15 (.D(RegIn[14]), .clk(and_1_out), .Q(RegOut[14]), .reset(Reset));  // open: Qn, preset
  D_Flip_Flop d_ff_16 (.D(RegIn[15]), .clk(and_1_out), .Q(RegOut[15]), .reset(Reset));  // open: Qn, preset

  // Other names for the same wires on the sheet: gEnable = globalEnable; B0 = RegIn[0]; B1 = RegIn[1]; B2 = RegIn[2];
  //   B3 = RegIn[3]; B4 = RegIn[4]; B5 = RegIn[5]; B6 = RegIn[6]; B7 = RegIn[7]; B8 = RegIn[8]; B9 = RegIn[9];
  //   B10 = RegIn[10]; B11 = RegIn[11]; B12 = RegIn[12]; B13 = RegIn[13]; B14 = RegIn[14]; B15 = RegIn[15];
  //   o0 = RegOut[0]; o1 = RegOut[1]; o2 = RegOut[2]; o3 = RegOut[3]; o4 = RegOut[4]; o5 = RegOut[5]; o6 = RegOut[6];
  //   o7 = RegOut[7]; o8 = RegOut[8]; o9 = RegOut[9]; o10 = RegOut[10]; o11 = RegOut[11]; o12 = RegOut[12];
  //   o13 = RegOut[13]; o14 = RegOut[14]; o15 = RegOut[15]
endmodule

module memory_latch (
  input  [15:0] address,
  input  WE,
  input  clk,
  input  [15:0] data_in,
  output [15:0] address_latched,
  output WE_latched,
  output OE_latched,
  output [15:0] data_in_latched
);

  wire DMwe_latch_q;
  wire [15:0] addr_latch_q;

  Register #(.width(16), .trigger("falling")) addr_latch (
    .D(address), .en(WE), .clk(clk), .Q(addr_latch_q));  // open: clr
  D_Flip_Flop #(.trigger("falling")) DMwe_latch (.D(WE), .clk(clk), .Q(DMwe_latch_q));  // open: Qn, preset, reset
  Register #(.width(16), .trigger("falling")) data_to_be_written (
    .D(data_in), .en(WE), .clk(clk), .Q(data_in_latched));  // open: clr
  Multiplexer #(.width(16), .enable("false")) multiplexer_1 (
    .in0(address), .in1(addr_latch_q), .out(address_latched), .sel(DMwe_latch_q));
  and and_1 (WE_latched, clk, DMwe_latch_q);
  not not_1 (OE_latched, WE_latched);
endmodule

module pcDecoder (
  input  [15:0] Instruction,
  output [3:0] opCode,
  output [11:0] Address,
  output [5:0] Immediate,
  output [2:0] Rt,
  output [2:0] Shamt,
  output [2:0] Rd,
  output [2:0] Rs
);

  wire and_1_out, and_2_out, and_3_out, and_4_out, and_5_out, and_6_out, and_7_out, and_8_out, and_9_out,
       and_10_out, and_11_out, and_12_out, enI, enJ, enR, not_1_out, not_2_out, not_3_out, not_4_out,
       not_5_out, not_6_out, not_7_out, not_8_out, not_9_out, not_10_out, not_11_out, not_12_out, not_13_out,
       not_14_out, not_15_out, not_16_out, not_17_out, not_18_out, not_19_out;

  not not_1 (not_1_out, Instruction[13]);
  not not_2 (not_2_out, Instruction[14]);
  not not_3 (not_3_out, Instruction[13]);
  not not_4 (not_4_out, Instruction[14]);
  not not_5 (not_5_out, Instruction[13]);
  not not_6 (not_6_out, Instruction[14]);
  not not_7 (not_7_out, Instruction[12]);
  not not_8 (not_8_out, Instruction[14]);
  not not_9 (not_9_out, Instruction[12]);
  not not_10 (not_10_out, Instruction[13]);
  not not_11 (not_11_out, Instruction[12]);
  not not_12 (not_12_out, Instruction[13]);
  not not_13 (not_13_out, Instruction[15]);
  not not_14 (not_14_out, Instruction[14]);
  not not_15 (not_15_out, Instruction[15]);
  not not_16 (not_16_out, Instruction[12]);
  not not_17 (not_17_out, Instruction[15]);
  not not_18 (not_18_out, Instruction[13]);
  not not_19 (not_19_out, Instruction[15]);
  and and_1 (and_1_out, Instruction[12], not_1_out, Instruction[14], Instruction[15]);
  and and_2 (and_2_out, Instruction[12], Instruction[13], not_2_out, Instruction[15]);
  and and_3 (and_3_out, not_3_out, not_4_out, Instruction[15]);
  and and_4 (and_4_out, Instruction[12], not_5_out, not_6_out);
  and and_5 (and_5_out, Instruction[12], Instruction[13], Instruction[14]);
  and and_6 (and_6_out, Instruction[13], Instruction[14], Instruction[15]);
  and and_7 (and_7_out, not_7_out, Instruction[13], not_8_out, Instruction[15]);
  // NOT_Gate not_20 has open pins: in=Instruction[15], out=open
  and and_8 (and_8_out, not_9_out, not_10_out, Instruction[14], Instruction[15]);
  and and_9 (and_9_out, not_11_out, not_12_out, not_13_out);
  and and_10 (and_10_out, Instruction[13], not_14_out, not_15_out);
  and and_11 (and_11_out, not_16_out, Instruction[13], not_17_out);
  and and_12 (and_12_out, Instruction[12], not_18_out, Instruction[14], not_19_out);
  or J (enJ, and_1_out, and_2_out);
  or I (enI, and_3_out, and_4_out, and_5_out, and_6_out, and_7_out);
  or R (enR, and_8_out, and_9_out, and_10_out, and_11_out, and_12_out);
  assign Address = enJ ? Instruction[11:0] : 12'bz;  // Controlled_Buffer controlled_buffer_1
  assign {Rs, Rt, Immediate} = enI ? Instruction[11:0] : 12'bz;  // Controlled_Buffer controlled_buffer_2
  assign {Rs, Rt, Rd, Shamt} = enR ? Instruction[11:0] : 12'bz;  // Controlled_Buffer controlled_buffer_3
  // Probe on nothing

  assign opCode = Instruction[15:12];

  // Other names for the same wires on the sheet: other[11:0] = Instruction[11:0]; rs1[2:0] = Rs; rs2[2:0] = Rs;
  //   rt1[2:0] = Rt; rt2[2:0] = Rt
endmodule

module immediateExt (
  input  [5:0] immediate,
  output [15:0] extended
);


  assign extended = {{11{immediate[5]}}, immediate[4:0]};
endmodule

module ZeroExt12 (
  input  [11:0] bitsIn,
  output [15:0] bitsOut
);


  assign bitsOut = {4'b0000, bitsIn};
endmodule

module Control (
  input  [3:0] opCode,
  output Rwe,
  output Ble,
  output DMwe,
  output Jal,
  output Rwd,
  output Rdst,
  output [2:0] ALUop,
  output Jr,
  output Bne,
  output inputE,
  output Jp,
  output outputE,
  output ALUinB
);

  wire and_1_out, and_2_out, and_3_out, and_4_out, and_5_out, and_6_out, and_7_out, and_8_out, and_9_out,
       and_10_out, and_11_out, and_12_out, and_13_out, and_14_out, and_15_out, and_19_out, and_20_out,
       not_1_out, not_2_out, not_3_out, not_4_out, not_5_out, not_6_out, not_7_out, not_8_out, not_9_out,
       not_10_out, not_11_out, not_12_out, not_13_out, not_14_out, not_15_out, not_16_out, not_17_out,
       not_18_out, not_19_out, not_20_out, not_21_out, not_22_out, not_23_out, not_24_out, not_25_out,
       not_26_out, not_27_out, not_28_out, not_29_out, not_30_out, not_31_out, not_32_out, not_33_out,
       not_34_out, not_35_out, not_36_out, not_37_out, not_38_out, not_39_out, not_40_out, not_41_out,
       not_42_out, not_43_out, not_44_out, not_45_out;

  not not_1 (not_1_out, opCode[3]);
  not not_2 (not_2_out, opCode[1]);
  not not_3 (not_3_out, opCode[3]);
  not not_4 (not_4_out, opCode[0]);
  not not_5 (not_5_out, opCode[3]);
  not not_6 (not_6_out, opCode[2]);
  not not_7 (not_7_out, opCode[3]);
  not not_8 (not_8_out, opCode[1]);
  not not_9 (not_9_out, opCode[0]);
  not not_10 (not_10_out, opCode[2]);
  not not_11 (not_11_out, opCode[1]);
  not not_12 (not_12_out, opCode[2]);
  not not_13 (not_13_out, opCode[0]);
  not not_14 (not_14_out, opCode[3]);
  not not_15 (not_15_out, opCode[0]);
  and and_1 (and_1_out, not_1_out, opCode[2], not_2_out, opCode[0]);
  and and_2 (and_2_out, not_3_out, opCode[2], opCode[1], not_4_out);
  and and_3 (and_3_out, not_5_out, not_6_out, opCode[1], opCode[0]);
  and and_4 (and_4_out, not_7_out, opCode[2], not_8_out, not_9_out);
  and and_5 (and_5_out, opCode[3], not_10_out, not_11_out, opCode[0]);
  and and_6 (and_6_out, not_12_out, opCode[1], not_13_out);
  and and_7 (and_7_out, not_14_out, opCode[2], not_15_out);
  or b2 (ALUop[2], and_1_out, and_2_out);
  or b1 (ALUop[1], and_3_out, and_4_out);
  or b0 (ALUop[0], and_5_out, and_6_out, and_7_out);
  not not_16 (not_16_out, opCode[1]);
  not not_17 (not_17_out, opCode[0]);
  not not_18 (not_18_out, opCode[3]);
  not not_19 (not_19_out, opCode[2]);
  not not_20 (not_20_out, opCode[3]);
  not not_21 (not_21_out, opCode[1]);
  not not_22 (not_22_out, opCode[3]);
  not not_23 (not_23_out, opCode[0]);
  not not_24 (not_24_out, opCode[3]);
  not not_25 (not_25_out, opCode[2]);
  not not_26 (not_26_out, opCode[1]);
  not not_27 (not_27_out, opCode[3]);
  not not_28 (not_28_out, opCode[2]);
  not not_29 (not_29_out, opCode[1]);
  not not_30 (not_30_out, opCode[0]);
  not not_31 (not_31_out, opCode[3]);
  and and_8 (and_8_out, opCode[2], not_16_out, opCode[0]);
  and and_9 (and_9_out, opCode[2], opCode[1], not_17_out);
  and and_10 (and_10_out, not_18_out, not_19_out, opCode[1]);
  and and_11 (and_11_out, not_20_out, opCode[2], not_21_out);
  and and_12 (and_12_out, not_22_out, not_23_out);
  and and_13 (and_13_out, not_24_out, not_25_out, not_26_out, opCode[0]);
  and and_14 (and_14_out, not_27_out, opCode[2], opCode[1], opCode[0]);
  and and_15 (and_15_out, opCode[3], not_28_out, not_29_out, not_30_out);
  or or_1 (Rwe, not_31_out, and_8_out, and_9_out);
  or or_2 (Rdst, and_10_out, and_11_out, and_12_out);
  or or_3 (ALUinB, and_13_out, and_14_out, and_15_out);
  not not_32 (not_32_out, opCode[2]);
  and and_16 (DMwe, opCode[3], not_32_out, not_33_out, not_34_out);
  not not_33 (not_33_out, opCode[1]);
  not not_34 (not_34_out, opCode[0]);
  not not_35 (not_35_out, opCode[3]);
  and and_17 (Rwd, not_35_out, opCode[2], opCode[1], opCode[0]);
  not not_36 (not_36_out, opCode[2]);
  and and_18 (Bne, opCode[3], not_36_out, not_37_out, opCode[0]);
  not not_37 (not_37_out, opCode[1]);
  not not_38 (not_38_out, opCode[2]);
  and and_19 (and_19_out, opCode[3], not_38_out, opCode[1], opCode[0]);
  and and_20 (and_20_out, opCode[3], opCode[2], not_39_out, opCode[0]);
  not not_39 (not_39_out, opCode[1]);
  or or_4 (Jp, and_19_out, and_20_out);
  not not_40 (not_40_out, opCode[2]);
  and and_21 (Ble, opCode[3], not_40_out, opCode[1], not_41_out);
  not not_41 (not_41_out, opCode[0]);
  and and_22 (Jal, opCode[3], opCode[2], not_42_out, opCode[0]);
  not not_42 (not_42_out, opCode[1]);
  and and_23 (Jr, opCode[3], opCode[2], not_43_out, not_44_out);
  not not_43 (not_43_out, opCode[1]);
  not not_44 (not_44_out, opCode[0]);
  and and_24 (inputE, opCode[3], opCode[2], opCode[1], not_45_out);
  not not_45 (not_45_out, opCode[0]);
  and and_25 (outputE, opCode[3], opCode[2], opCode[1], opCode[0]);

  // Other names for the same wires on the sheet: d = opCode[0]; c = opCode[1]; b = opCode[2]; a = opCode[3]
endmodule

module OutputRead (
  input  [15:0] Rs,
  output [6:0] RsOut
);


  assign RsOut = Rs[6:0];
endmodule

module ZeroExt7 (
  input  [6:0] in7,
  input  text,
  output [15:0] out12
);

  wire text_t;
  wire [6:6] not_2_out;

  not not_1 (text_t, text);
  not not_2 (not_2_out[6], text_t);
  Multiplexer #(.width(16), .enable("false")) multiplexer_1 (
    .in0({{8{1'b0}}, text_t, in7}), .in1({{8{1'b0}}, text_t, {7{not_2_out[6]}}}), .out(out12), .sel(text_t));
endmodule
