// Logisim project my_adder.circ as structural Verilog: 2 circuits, main circuit main
module main (
  input  [15:0] A,
  input  sub,
  input  [15:0] B,
  output [15:0] result,
  output ovf
);

  wire B0, B1, B2, B3, B4, B5, B6, B7, B8, B9, B10, B11, B12, B13, B14, B15, bitadd_1_cout, bitadd_2_cout,
       bitadd_3_cout, bitadd_4_cout, bitadd_5_cout, bitadd_6_cout, bitadd_7_cout, bitadd_8_cout,
       bitadd_9_cout, bitadd_10_cout, bitadd_11_cout, bitadd_12_cout, bitadd_13_cout, bitadd_14_cout,
       bitadd_15_cout, bitadd_16_cout;
  wire [15:0] not_1_out;

  assign not_1_out = ~B;  // NOT_Gate not_1, 16 bits wide
  Multiplexer #(.width(16), .enable("false")) multiplexer_1 (
    .in0(B), .in1(not_1_out), .out({B15, B14, B13, B12, B11, B10, B9, B8, B7, B6, B5, B4, B3, B2, B1, B0}),
    .sel(sub));
  bitAdd bitadd_1 (.sum(result[0]), .cIN(sub), .cOUT(bitadd_1_cout), .B(B0), .A(A[0]));
  bitAdd bitadd_2 (.sum(result[1]), .cIN(bitadd_1_cout), .cOUT(bitadd_2_cout), .B(B1), .A(A[1]));
  bitAdd bitadd_3 (.sum(result[2]), .cIN(bitadd_2_cout), .cOUT(bitadd_3_cout), .B(B2), .A(A[2]));
  bitAdd bitadd_4 (.sum(result[3]), .cIN(bitadd_3_cout), .cOUT(bitadd_4_cout), .B(B3), .A(A[3]));
  bitAdd bitadd_5 (.sum(result[4]), .cIN(bitadd_4_cout), .cOUT(bitadd_5_cout), .B(B4), .A(A[4]));
  bitAdd bitadd_6 (.sum(result[5]), .cIN(bitadd_5_cout), .cOUT(bitadd_6_cout), .B(B5), .A(A[5]));
  bitAdd bitadd_7 (.sum(result[6]), .cIN(bitadd_6_cout), .cOUT(bitadd_7_cout), .B(B6), .A(A[6]));
  bitAdd bitadd_8 (.sum(result[7]), .cIN(bitadd_7_cout), .cOUT(bitadd_8_cout), .B(B7), .A(A[7]));
  bitAdd bitadd_9 (.sum(result[8]), .cIN(bitadd_8_cout), .cOUT(bitadd_9_cout), .B(B8), .A(A[8]));
  bitAdd bitadd_10 (.sum(result[9]), .cIN(bitadd_9_cout), .cOUT(bitadd_10_cout), .B(B9), .A(A[9]));
  bitAdd bitadd_11 (.sum(result[10]), .cIN(bitadd_10_cout), .cOUT(bitadd_11_cout), .B(B10), .A(A[10]));
  bitAdd bitadd_12 (.sum(result[11]), .cIN(bitadd_11_cout), .cOUT(bitadd_12_cout), .B(B11), .A(A[11]));
  bitAdd bitadd_13 (.sum(result[12]), .cIN(bitadd_12_cout), .cOUT(bitadd_13_cout), .B(B12), .A(A[12]));
  bitAdd bitadd_14 (.sum(result[13]), .cIN(bitadd_13_cout), .cOUT(bitadd_14_cout), .B(B13), .A(A[13]));
  bitAdd bitadd_15 (.sum(result[14]), .cIN(bitadd_14_cout), .cOUT(bitadd_15_cout), .B(B14), .A(A[14]));
  bitAdd bitadd_16 (.sum(result[15]), .cIN(bitadd_15_cout), .cOUT(bitadd_16_cout), .B(B15), .A(A[15]));
  xor xor_1 (ovf, bitadd_15_cout, bitadd_16_cout);

  // Other names for the same wires on the sheet: check = sub; o0 = result[0]; o1 = result[1]; o2 = result[2];
  //   o3 = result[3]; o4 = result[4]; o5 = result[5]; o6 = result[6]; o7 = result[7]; o8 = result[8]; o9 = result[9];
  //   o10 = result[10]; o11 = result[11]; o12 = result[12]; o13 = result[13]; o14 = result[14]; o15 = result[15]
endmodule

module bitAdd (
  input  A,
  input  B,
  input  cIN,
  output cOUT,
  output sum
);

  wire and_1_out, and_2_out, xor_1_out;

  xor xor_1 (xor_1_out, A, B);
  and and_1 (and_1_out, A, B);
  and and_2 (and_2_out, xor_1_out, cIN);
  xor xor_2 (sum, xor_1_out, cIN);
  or or_1 (cOUT, and_1_out, and_2_out);
endmodule
