// Logisim project press.circ as structural Verilog: 1 circuit, main circuit main
module main (
  input  go,
  input  limit,
  output warning,
  output motor
);

  wire clk, eight_out, five_out, four_out, nine_out, not_1_out, not_2_out, not_3_out, not_4_out, not_5_out,
       not_6_out, not_7_out, not_8_out, not_9_out, not_10_out, not_11_out, not_12_out, or_1_out, or_2_out,
       Q0_q, Q1_q, seven_out, six_out, three_out, two_out;

  not not_1 (not_1_out, limit);
  not not_2 (not_2_out, Q0_q);
  not not_3 (not_3_out, go);
  not not_4 (not_4_out, Q1_q);
  not not_5 (not_5_out, limit);
  not not_6 (not_6_out, Q1_q);
  not not_7 (not_7_out, Q1_q);
  not not_8 (not_8_out, Q0_q);
  not not_9 (not_9_out, Q1_q);
  not not_10 (not_10_out, go);
  not not_11 (not_11_out, Q0_q);
  not not_12 (not_12_out, Q0_q);
  and five (five_out, go, not_1_out, not_2_out, Q1_q);
  and six (six_out, not_3_out, Q0_q, not_4_out);
  and seven (seven_out, go, not_5_out, Q0_q, not_6_out);
  and eight (eight_out, go, limit, Q0_q, not_7_out);
  and nine (nine_out, go, Q0_q, Q1_q);
  and two (two_out, go, not_8_out, not_9_out);
  and three (three_out, not_10_out, not_11_out, Q1_q);
  and four (four_out, go, limit, not_12_out, Q1_q);
  or or_1 (or_1_out, five_out, six_out, seven_out, eight_out, nine_out);
  or or_2 (or_2_out, nine_out, eight_out, two_out, three_out, four_out);
  or or_3 (motor, two_out, four_out, five_out, seven_out);
  or or_4 (warning, five_out, six_out, seven_out, eight_out, nine_out, two_out, three_out, four_out);
  Clock clock_1 (.out(clk));
  D_Flip_Flop Q0 (.D(or_1_out), .clk(clk), .Q(Q0_q));  // open: Qn, preset, reset
  D_Flip_Flop Q1 (.D(or_2_out), .clk(clk), .Q(Q1_q));  // open: Qn, preset, reset
endmodule
